# Fritzing sketch cheTempoFa-0.1 (saved by Fritzing 0.9.3b)
circuit board: 8.46667cm x 5.64444cm
breadboards: 1

parts:
  U1 = ESP8266 WiFi Module [part_number=ESP8266]
  R1 = Resistor [tolerance=±5% resistance=3.3k package=THT]
  R2 = Resistor [tolerance=±5% resistance=3.3k package=THT]
  R3 = Resistor [tolerance=±5% resistance=3.3k package=THT]
  R4 = Resistor [tolerance=±5% resistance=3.3k package=THT]
  R5 = Resistor [tolerance=±5% resistance=330 package=THT]
  R6 = Resistor [tolerance=±5% resistance=330 package=THT]
  OLED1 = OLED 128x64 I2C Monochrome Display
  HLK-PM1 = HLK-PM01
  JP1 = Header 2 [package=screwterminal-3.5mm-2_lock]
  J1 = male pin header, 6 pins [form="♂ (male)"]
  S1_reset = Momentary Switch [package=ksa_sealed_tac_switch]
  S2_Function = Momentary Switch [package=ksa_sealed_tac_switch]
  J2 = male pin header, 2 pins [form="♂ (male)"]

nets:
  N1: U1.RXD, J1.pin4, S1_reset.3, S1_reset.4
  VCC: U1.VCC, R1.Pin_1, R2.Pin_1, R3.Pin_1, R4.Pin_1, OLED1.VDD, HLK-PM1.+Vo, J1.pin3
  N2: U1.GPIO_0, R1.Pin_0, R5.Pin_1, J2.pin2
  N3: U1.GPIO_16, R3.Pin_0, S2_Function.4
  N4: U1.GPIO_2, R2.Pin_0, R6.Pin_1
  N5: U1.CH_PD, R4.Pin_0
  GND: U1.GND, OLED1.GND, HLK-PM1.-Vo, J1.pin1, S1_reset.1, S1_reset.2, S2_Function.1, S2_Function.2, J2.pin1
  N6: U1.TXD, J1.pin5
  N7: R5.Pin_0, OLED1.SDA
  N8: R6.Pin_0, OLED1.SCK
  N9: HLK-PM1.AC#0, JP1.2
  N10: HLK-PM1.AC#1, JP1.1

custom parts:
  ESP8266 WiFi Module: Generic WiFi Module based on the ESP8266 with onboard PCB antenna and UART communications
  HLK-PM01: AC-DC 220V to 5V Step-Down Power Supply Module
